// Logisim project 1.circ as structural Verilog
// LED计数
module \LED计数电路  (
  input  In1,
  input  In2,
  input  In3,
  input  In4,
  input  In5,
  output Out1,
  output Out2,
  output Out3,
  output Out4,
  output Out5
);

  or or_1 (Out1, In1, In2, In3, In4, In5);
  or or_2 (Out2, In2, In3, In4, In5);
  or or_3 (Out3, In3, In4, In5);
  or or_4 (Out4, In4, In5);

  assign Out5 = In5;
endmodule

module \LED计数测试  (
);

  wire button_1_out, button_2_out, button_3_out, button_4_out, button_5_out, \led计数电路_1_out1 ,
       \led计数电路_1_out2 , \led计数电路_1_out3 , \led计数电路_1_out4 , \led计数电路_1_out5 ;

  Button button_1 (.out(button_1_out));
  Button button_2 (.out(button_2_out));
  Button button_3 (.out(button_3_out));
  Button button_4 (.out(button_4_out));
  Button button_5 (.out(button_5_out));
  \LED计数电路  \led计数电路_1  (
    .In1(button_1_out), .In2(button_2_out), .In3(button_3_out), .In4(button_4_out), .In5(button_5_out),
    .Out1(\led计数电路_1_out1 ), .Out2(\led计数电路_1_out2 ), .Out3(\led计数电路_1_out3 ), .Out4(\led计数电路_1_out4 ),
    .Out5(\led计数电路_1_out5 ));
  LED led_1 (.in(\led计数电路_1_out1 ));
  LED led_2 (.in(\led计数电路_1_out2 ));
  LED led_3 (.in(\led计数电路_1_out3 ));
  LED led_4 (.in(\led计数电路_1_out4 ));
  LED led_5 (.in(\led计数电路_1_out5 ));
endmodule

module \_5输入按键编码器设计  (
  input  In1,
  input  In2,
  input  In3,
  input  In4,
  input  In5,
  output Out1,
  output Out2,
  output Out3
);

  wire and_1_out, and_2_out, and_3_out, and_4_out, not_1_out, not_2_out, not_3_out, not_4_out, not_5_out,
       not_6_out, not_7_out;

  not not_1 (not_1_out, In4);
  not not_2 (not_2_out, In2);
  not not_3 (not_3_out, In4);
  not not_4 (not_4_out, In4);
  not not_5 (not_5_out, In5);
  not not_6 (not_6_out, In4);
  not not_7 (not_7_out, In5);
  or or_1 (Out3, In5, In4);
  and and_1 (and_1_out, In3, not_1_out);
  and and_2 (and_2_out, In1, not_2_out, not_3_out);
  and and_3 (and_3_out, In3, not_4_out, not_5_out);
  and and_4 (and_4_out, In2, not_6_out, not_7_out);
  or or_2 (Out1, In5, and_1_out, and_2_out);
  or or_3 (Out2, and_3_out, and_4_out);
endmodule

module \_5输入编码电路测试  (
);

  wire button_1_out, button_2_out, button_3_out, button_4_out, button_5_out, \led计数电路_1_out1 ,
       \led计数电路_1_out2 , \led计数电路_1_out3 , \led计数电路_1_out4 , \led计数电路_1_out5 ;
  wire [2:0] \n5输入按键编码器设计_1_out1 ;

  Button button_1 (.out(button_1_out));
  Button button_2 (.out(button_2_out));
  Button button_3 (.out(button_3_out));
  Button button_4 (.out(button_4_out));
  Button button_5 (.out(button_5_out));
  \LED计数电路  \led计数电路_1  (
    .In1(button_1_out), .In2(button_2_out), .In3(button_3_out), .In4(button_4_out), .In5(button_5_out),
    .Out1(\led计数电路_1_out1 ), .Out2(\led计数电路_1_out2 ), .Out3(\led计数电路_1_out3 ), .Out4(\led计数电路_1_out4 ),
    .Out5(\led计数电路_1_out5 ));
  \_5输入按键编码器设计  \u_5输入按键编码器设计_1  (
    .In1(button_1_out), .In2(button_2_out), .In3(button_3_out), .In4(button_4_out), .In5(button_5_out),
    .Out1(\n5输入按键编码器设计_1_out1 [0]), .Out2(\n5输入按键编码器设计_1_out1 [1]), .Out3(\n5输入按键编码器设计_1_out1 [2]));
  LED led_1 (.in(\led计数电路_1_out1 ));
  LED led_2 (.in(\led计数电路_1_out2 ));
  LED led_3 (.in(\led计数电路_1_out3 ));
  LED led_4 (.in(\led计数电路_1_out4 ));
  LED led_5 (.in(\led计数电路_1_out5 ));
  Hex_Digit_Display hex_digit_display_1 (.value({1'b0, \n5输入按键编码器设计_1_out1 }), .dp(1'b1));
endmodule

module \_7数码管显示驱动  (
  input  X3,
  input  X2,
  input  X1,
  input  X0,
  output Seg_1,
  output Seg_2,
  output Seg_3,
  output Seg_4,
  output Seg_5,
  output Seg_6,
  output Seg_7
);

  wire and_1_out, and_2_out, and_3_out, and_4_out, and_5_out, and_6_out, and_7_out, and_8_out, and_9_out,
       and_10_out, and_11_out, and_12_out, and_13_out, and_14_out, and_15_out, and_16_out, and_17_out,
       and_18_out, and_19_out, and_20_out, and_21_out, and_22_out, and_23_out, and_24_out, and_25_out,
       and_26_out, and_27_out, and_28_out, and_29_out, and_30_out, and_31_out, and_32_out, and_33_out,
       and_34_out, and_35_out, not_1_out, not_2_out, not_3_out, not_4_out, not_5_out, not_6_out, not_7_out,
       not_8_out, not_9_out, not_10_out, not_11_out, not_12_out, not_13_out, not_14_out, not_15_out,
       not_16_out, not_17_out, not_18_out, not_19_out, not_20_out, not_21_out, not_22_out, not_23_out,
       not_24_out, not_25_out, not_26_out, not_27_out, not_28_out, not_29_out, not_30_out, not_31_out,
       not_32_out, not_33_out, not_34_out, not_35_out, not_36_out, not_37_out, not_38_out, not_39_out,
       not_40_out, not_41_out, not_42_out, not_43_out, not_44_out;

  not not_1 (not_1_out, X2);
  and and_1 (and_1_out, not_1_out, X1);
  and and_2 (and_2_out, X1, not_2_out);
  not not_2 (not_2_out, X0);
  not not_3 (not_3_out, X3);
  and and_3 (and_3_out, not_3_out, X2, not_4_out);
  not not_4 (not_4_out, X1);
  and and_4 (and_4_out, X3, not_5_out);
  not not_5 (not_5_out, X2);
  and and_5 (and_5_out, X3, X0);
  not not_6 (not_6_out, X1);
  and and_6 (and_6_out, not_6_out, not_7_out);
  not not_7 (not_7_out, X0);
  not not_8 (not_8_out, X3);
  and and_7 (and_7_out, not_8_out, X2, not_9_out);
  not not_9 (not_9_out, X1);
  and and_8 (and_8_out, X2, not_10_out);
  not not_10 (not_10_out, X0);
  and and_9 (and_9_out, X3, not_11_out);
  not not_11 (not_11_out, X2);
  and and_10 (and_10_out, X3, X1);
  not not_12 (not_12_out, X2);
  and and_11 (and_11_out, not_12_out, not_13_out);
  not not_13 (not_13_out, X0);
  not not_14 (not_14_out, X3);
  and and_12 (and_12_out, not_14_out, X1);
  not not_15 (not_15_out, X3);
  and and_13 (and_13_out, not_15_out, X2, X0);
  and and_14 (and_14_out, X2, X1);
  not not_16 (not_16_out, X2);
  and and_15 (and_15_out, X3, not_16_out, not_17_out);
  not not_17 (not_17_out, X1);
  and and_16 (and_16_out, X3, not_18_out);
  not not_18 (not_18_out, X0);
  not not_19 (not_19_out, X3);
  and and_17 (and_17_out, not_19_out, not_20_out);
  not not_20 (not_20_out, X2);
  not not_21 (not_21_out, X3);
  not not_22 (not_22_out, X1);
  and and_18 (and_18_out, not_21_out, not_22_out, not_23_out);
  not not_23 (not_23_out, X0);
  not not_24 (not_24_out, X2);
  and and_19 (and_19_out, not_24_out, not_25_out);
  not not_25 (not_25_out, X0);
  not not_26 (not_26_out, X3);
  and and_20 (and_20_out, not_26_out, X1, X0);
  not not_27 (not_27_out, X1);
  and and_21 (and_21_out, X3, not_27_out, X0);
  not not_28 (not_28_out, X2);
  and and_22 (and_22_out, not_28_out, not_29_out);
  not not_29 (not_29_out, X0);
  and and_23 (and_23_out, X1, not_30_out);
  not not_30 (not_30_out, X0);
  and and_24 (and_24_out, X3, X1);
  and and_25 (and_25_out, X3, X2);
  not not_31 (not_31_out, X3);
  not not_32 (not_32_out, X2);
  and and_26 (and_26_out, not_31_out, not_32_out, not_33_out);
  not not_33 (not_33_out, X0);
  not not_34 (not_34_out, X2);
  and and_27 (and_27_out, not_34_out, X1, X0);
  not not_35 (not_35_out, X1);
  and and_28 (and_28_out, X2, not_35_out, X0);
  and and_29 (and_29_out, X2, X1, not_36_out);
  not not_36 (not_36_out, X0);
  not not_37 (not_37_out, X1);
  and and_30 (and_30_out, X3, not_37_out, not_38_out);
  not not_38 (not_38_out, X0);
  not not_39 (not_39_out, X3);
  and and_31 (and_31_out, not_39_out, not_40_out);
  not not_40 (not_40_out, X1);
  not not_41 (not_41_out, X3);
  and and_32 (and_32_out, not_41_out, X0);
  not not_42 (not_42_out, X1);
  and and_33 (and_33_out, not_42_out, X0);
  not not_43 (not_43_out, X3);
  and and_34 (and_34_out, not_43_out, X2);
  and and_35 (and_35_out, X3, not_44_out);
  not not_44 (not_44_out, X2);
  or or_1 (Seg_1, and_1_out, and_2_out, and_3_out, and_4_out, and_5_out);
  or or_2 (Seg_2, and_6_out, and_7_out, and_8_out, and_9_out, and_10_out);
  or or_3 (Seg_4, and_17_out, and_18_out, and_19_out, and_20_out, and_21_out);
  or or_4 (Seg_5, and_22_out, and_23_out, and_24_out, and_25_out);
  or or_5 (Seg_6, and_26_out, and_27_out, and_28_out, and_29_out, and_30_out);
  or or_6 (Seg_7, and_31_out, and_32_out, and_33_out, and_34_out, and_35_out);
  or or_7 (Seg_3, and_11_out, and_12_out, and_13_out, and_14_out, and_15_out, and_16_out);
endmodule

module \数码管驱动自动测试  (
);

  wire clock_1_out, \n7数码管显示驱动_1_seg_1 , \n7数码管显示驱动_1_seg_2 , \n7数码管显示驱动_1_seg_3 , \n7数码管显示驱动_1_seg_4 ,
       \n7数码管显示驱动_1_seg_5 , \n7数码管显示驱动_1_seg_6 , \n7数码管显示驱动_1_seg_7 ;
  wire [3:0] counter_1_q;

  Clock clock_1 (.out(clock_1_out));
  Counter #(.width(4), .max('hf)) counter_1 (
    .Q(counter_1_q), .clk(clock_1_out));  // open: load, D, count, carry, clr, preset, down
  \_7数码管显示驱动  \u_7数码管显示驱动_1  (
    .X3(counter_1_q[3]), .X2(counter_1_q[2]), .X1(counter_1_q[1]), .X0(counter_1_q[0]),
    .Seg_1(\n7数码管显示驱动_1_seg_1 ), .Seg_2(\n7数码管显示驱动_1_seg_2 ), .Seg_3(\n7数码管显示驱动_1_seg_3 ),
    .Seg_4(\n7数码管显示驱动_1_seg_4 ), .Seg_5(\n7数码管显示驱动_1_seg_5 ), .Seg_6(\n7数码管显示驱动_1_seg_6 ),
    .Seg_7(\n7数码管显示驱动_1_seg_7 ));
  _7_Segment_Display u_7_segment_display_1 (
    .g(\n7数码管显示驱动_1_seg_1 ), .f(\n7数码管显示驱动_1_seg_2 ), .a(\n7数码管显示驱动_1_seg_3 ), .b(\n7数码管显示驱动_1_seg_4 ),
    .e(\n7数码管显示驱动_1_seg_5 ), .d(\n7数码管显示驱动_1_seg_6 ), .c(\n7数码管显示驱动_1_seg_7 ));  // open: dp
endmodule

module \集成到LED计数测试电路  (
);

  wire button_1_out, button_2_out, button_3_out, button_4_out, button_5_out, \led计数电路_1_out1 ,
       \led计数电路_1_out2 , \led计数电路_1_out3 , \led计数电路_1_out4 , \led计数电路_1_out5 , \n7数码管显示驱动_1_seg_1 ,
       \n7数码管显示驱动_1_seg_2 , \n7数码管显示驱动_1_seg_3 , \n7数码管显示驱动_1_seg_4 , \n7数码管显示驱动_1_seg_5 ,
       \n7数码管显示驱动_1_seg_6 , \n7数码管显示驱动_1_seg_7 ;
  wire [2:0] \n5输入按键编码器设计_1_out1 ;

  Button button_1 (.out(button_1_out));
  Button button_2 (.out(button_2_out));
  Button button_3 (.out(button_3_out));
  Button button_4 (.out(button_4_out));
  Button button_5 (.out(button_5_out));
  \_5输入按键编码器设计  \u_5输入按键编码器设计_1  (
    .In1(button_1_out), .In2(button_2_out), .In3(button_3_out), .In4(button_4_out), .In5(button_5_out),
    .Out1(\n5输入按键编码器设计_1_out1 [0]), .Out2(\n5输入按键编码器设计_1_out1 [1]), .Out3(\n5输入按键编码器设计_1_out1 [2]));
  \LED计数电路  \led计数电路_1  (
    .In1(button_1_out), .In2(button_2_out), .In3(button_3_out), .In4(button_4_out), .In5(button_5_out),
    .Out1(\led计数电路_1_out1 ), .Out2(\led计数电路_1_out2 ), .Out3(\led计数电路_1_out3 ), .Out4(\led计数电路_1_out4 ),
    .Out5(\led计数电路_1_out5 ));
  LED led_1 (.in(\led计数电路_1_out1 ));
  LED led_2 (.in(\led计数电路_1_out2 ));
  LED led_3 (.in(\led计数电路_1_out3 ));
  LED led_4 (.in(\led计数电路_1_out4 ));
  LED led_5 (.in(\led计数电路_1_out5 ));
  Hex_Digit_Display hex_digit_display_1 (.value({1'b0, \n5输入按键编码器设计_1_out1 }), .dp(1'b1));
  \_7数码管显示驱动  \u_7数码管显示驱动_1  (
    .X3(1'b0), .X2(\n5输入按键编码器设计_1_out1 [2]), .X1(\n5输入按键编码器设计_1_out1 [1]), .X0(\n5输入按键编码器设计_1_out1 [0]),
    .Seg_1(\n7数码管显示驱动_1_seg_1 ), .Seg_2(\n7数码管显示驱动_1_seg_2 ), .Seg_3(\n7数码管显示驱动_1_seg_3 ),
    .Seg_4(\n7数码管显示驱动_1_seg_4 ), .Seg_5(\n7数码管显示驱动_1_seg_5 ), .Seg_6(\n7数码管显示驱动_1_seg_6 ),
    .Seg_7(\n7数码管显示驱动_1_seg_7 ));
  _7_Segment_Display u_7_segment_display_1 (
    .g(\n7数码管显示驱动_1_seg_1 ), .f(\n7数码管显示驱动_1_seg_2 ), .a(\n7数码管显示驱动_1_seg_3 ), .b(\n7数码管显示驱动_1_seg_4 ),
    .e(\n7数码管显示驱动_1_seg_5 ), .d(\n7数码管显示驱动_1_seg_6 ), .c(\n7数码管显示驱动_1_seg_7 ));  // open: dp
endmodule
